// Logisim project alistirma-3.8-akilli-kapi-kilidi.circ as structural Verilog: 1 circuit, main circuit alistirma-3.8-akilli-kapi-kilidi
module alistirma_3_8_akilli_kapi_kilidi (
  input  A,
  input  B,
  input  C,
  input  D,
  output out_5,
  output out_6
);

  wire A_prime_B_prime_out, A_prime_C_prime_out, A_prime_D_out, B_prime_C_prime_out, B_prime_D_out,
       C_prime_D_out, not_1_out, not_2_out, not_3_out, not_4_out;

  not not_1 (not_1_out, A);
  not not_2 (not_2_out, C);
  not not_3 (not_3_out, B);
  not not_4 (not_4_out, D);
  and A_prime_C_prime (A_prime_C_prime_out, not_1_out, not_2_out);
  and B_prime_C_prime (B_prime_C_prime_out, not_3_out, not_2_out);
  and A_prime_D (A_prime_D_out, not_1_out, D);
  and B_prime_D (B_prime_D_out, not_3_out, D);
  or A_prime_B_prime (A_prime_B_prime_out, not_1_out, not_3_out);
  or C_prime_D (C_prime_D_out, not_2_out, D);
  or F (out_5, A_prime_C_prime_out, B_prime_C_prime_out, A_prime_D_out, B_prime_D_out);
  and F_2 (out_6, A_prime_B_prime_out, C_prime_D_out);

  // Notes on the sheet:
  //   Minimal SOP ve POS değerlerini bulup, devrelerini tasarlayalım.
  //   F = A'C' + B'C' + A'D + B'D
  //   F = (A' + B')(C + D')
  //   F(A, B, C, D) = Σ(0,1,3,4,5,7,8,9,11)
  //   F(A, B, C, D) = π(2,6,10,12,13,14,15)
  //   Problem: Akıllı bir kapı kilidi 4 durum bitiyle çalışıyor: 𝐴 (gece modu aktif), 𝐵 (bakım modu aktif), 𝐶 (hareket sensörü tetiklendi), 𝐷 (yetkili kart okutuldu). Sistem şu iki durumdan herhangi birinde kapıyı kilitli tutuyor (𝐹 = 0): 
  //   hareket sensörü tetiklenmiş (𝐶 = 1) ama yetkili kart okutulmamışsa (𝐷 = 0), ya da gece modu ve bakım modu aynı anda aktifse (𝐴 = 1,𝐵 = 1,çakışan iki mod). Diğer tüm durumlarda kapı açık kalır (𝐹 = 1).
endmodule
