// Logisim project alistirma-3.9-otomatik-bahce-sulama-vanasi.circ as structural Verilog: 1 circuit, main circuit alistirma-3.9-otomatik-bahce-sulama-vanasi
module alistirma_3_9_otomatik_bahce_sulama_vanasi (
  input  A,
  input  B,
  input  C,
  input  D,
  output out_5,
  output out_6
);

  wire A_B_prime_D_prime_out, AB_out, B_D_out, B_prime_D_out, BD_prime_out, not_1_out, not_2_out, not_3_out,
       not_4_out;

  not not_1 (not_1_out, A);
  not not_2 (not_2_out, B);
  not not_3 (not_3_out, C);
  not not_4 (not_4_out, D);
  and B_prime_D (B_prime_D_out, not_2_out, D);
  and BD_prime (BD_prime_out, B, not_4_out);
  and AB (AB_out, A, B);
  or B_D (B_D_out, B, D);
  or A_B_prime_D_prime (A_B_prime_D_prime_out, A, not_2_out, not_4_out);
  or F (out_5, B_prime_D_out, BD_prime_out, AB_out);
  and F_2 (out_6, B_D_out, A_B_prime_D_prime_out);

  // Notes on the sheet:
  //   Diğer tüm durumlarda vana açılır (𝐹 = 1). Minimal SOP ve POS değerlerini bulup, devrelerini tasarlayalım.
  //   F = B'D + BD' + AB
  //   F(A, B, C, D) = π(0,2,5,7,8,10)
  //   F = (B + D)(A + B' + D')
  //   F(A, B, C, D) = Σ(1,3,4,6,9,11,12,13,14,15)
  //   Problem: Otomatik bir bahçe sulama vanası 4 sensör girişiyle çalışıyor: 𝐴 (gece modu aktif), 𝐵 (toprak nem sensörü, 1=toprak kuru), 𝐶 (yağmur sensörü), 𝐷 (zamanlayıcı te tiklendi). Vana şu iki durumda kapalı kalır (𝐹 = 0):
  //   ne toprak kuru ne de zamanlayıcı tetik lenmişse (𝐵 = 0,𝐷 = 0, sulamaya hiç gerek yok), ya da gündüz vakti (𝐴 = 0) toprak kuru ve zamanlayıcı tetiklenmiş olsa bile (𝐵 = 1,𝐷 = 1; öğle güneşinde sulama yaprak yanığına yol açabileceğinden engellenir).
endmodule
