// Logisim project ornek-3.12-endustriyel-kontrol-paneli.circ as structural Verilog: 1 circuit, main circuit ornek-3.12-endustriyel-kontrol-paneli
module ornek_3_12_endustriyel_kontrol_paneli (
  input  A,
  input  B,
  input  C,
  input  D,
  output out_5,
  output out_6
);

  wire A_prime_B_prime_out, A_prime_C_prime_D_out, B_prime_C_prime_out, B_prime_D_out, B_prime_D_prime_out,
       C_prime_D_prime_out, not_1_out, not_2_out, not_3_out, not_4_out;

  not not_1 (not_1_out, A);
  not not_2 (not_2_out, B);
  not not_3 (not_3_out, C);
  not not_4 (not_4_out, D);
  and B_prime_D_prime (B_prime_D_prime_out, not_2_out, not_4_out);
  and B_prime_C_prime (B_prime_C_prime_out, not_2_out, not_3_out);
  and A_prime_C_prime_D (A_prime_C_prime_D_out, not_1_out, not_3_out, D);
  or A_prime_B_prime (A_prime_B_prime_out, not_1_out, not_2_out);
  or C_prime_D_prime (C_prime_D_prime_out, not_3_out, not_4_out);
  or B_prime_D (B_prime_D_out, not_2_out, D);
  or F (out_5, B_prime_D_prime_out, B_prime_C_prime_out, A_prime_C_prime_D_out);
  and F_2 (out_6, A_prime_B_prime_out, C_prime_D_prime_out, B_prime_D_out);

  // Notes on the sheet:
  //   Minimal SOP ve POS değerlerini bulup, devrelerini tasarlayalım
  //   F(A, B, C, D) = Σ(0,1,2,5,8,9,10)
  //   F = B'D' + B'C' + A'C'D
  //   F = (A' + B')(C' + D')(B' + D)
  //   F(A, B, C, D) = π(3,4,6,7,11,12,13,14,15)
  //   Problem: 4 girişli bir endüstriyel kontrol panelinde 𝐴,𝐵,𝐶,𝐷 sinyalleri (1=aktif, 0=pasif) çeşitli sensör/anahtar durumlarını temsil ediyor. Sistem şu üç durumdan her hangi biri gerçekleştiğinde otomatik olarak güvenli moda geçip duruyor (𝐹 = 0):
  //   𝐵 aktifken 𝐷’nin pasif olması, 𝐴 ve 𝐵’nin ikisinin birden aktif olması (aşırı yük), ya da 𝐶 ve 𝐷’nin ikisinin birden aktif olması (çakışma).  Bu üç durumun hiçbiri gerçekleşmezse sistem normal çalışmada kalır (𝐹 = 1).
endmodule
