// Logisim project ornek-3.13-hata-kontrol-devresi.circ as structural Verilog: 1 circuit, main circuit ornek-3.13-hata-kontrol-devresi
module ornek_3_13_hata_kontrol_devresi (
  input  A,
  input  B,
  input  C,
  input  D,
  output out_5,
  output out_6
);

  wire A_B_out, AC_prime_out, AD_prime_out, BC_prime_out, BD_prime_out, C_prime_D_prime_out, not_1_out,
       not_2_out, not_3_out, not_4_out;

  not not_1 (not_1_out, A);
  not not_2 (not_2_out, B);
  not not_3 (not_3_out, C);
  not not_4 (not_4_out, D);
  and BC_prime (BC_prime_out, B, not_3_out);
  and BD_prime (BD_prime_out, B, not_4_out);
  and AC_prime (AC_prime_out, A, not_3_out);
  and AD_prime (AD_prime_out, A, not_4_out);
  or A_B (A_B_out, A, B);
  or C_prime_D_prime (C_prime_D_prime_out, not_3_out, not_4_out);
  or F (out_5, BC_prime_out, BD_prime_out, AC_prime_out, AD_prime_out);
  and F_2 (out_6, A_B_out, C_prime_D_prime_out);

  // Notes on the sheet:
  //   Bu iki durumdan herhangi biri gerçekleşirse çıkış 𝐹 = 0 (hata), aksi hâlde 𝐹 = 1 (normal) olsun. Minimal SOP ve POS değerlerini bulup, devrelerini tasarlayalım.
  //   F = BC' + BD' + AC' + AD'
  //   F(A, B, C, D) = π(0,1,2,3,7,11,15)
  //   F = (A + B)(C' + D')
  //   Problem: 4 bitlik bir kontrol kodu 𝐴𝐵𝐶𝐷, bir gömülü sistemde donanım durumunu temsil ediyor. Sistem tasarımcıları şu iki durumu hatalı kabul ediyor: 𝐴 ve 𝐵’nin ikisi de 0 olması, ya da 𝐶 ve𝐷’nin ikisi de 1 olması.
  //   F(A, B, C, D) = Σ(4,5,6,8,9,10,12,13,14)
endmodule
