// Logisim project alistirma-3.10-depo-sicaklik-gaz-alarmi.circ as structural Verilog: 1 circuit, main circuit alistirma-3.10-akilli-depo
module alistirma_3_10_akilli_depo (
  input  A,
  input  B,
  input  C,
  input  D,
  output F___C___ABD_prime,
  output out_6
);

  wire A_C_out, ABD_prime_out, B_C_out, not_1_out;

  not not_1 (not_1_out, D);
  and ABD_prime (ABD_prime_out, A, B, not_1_out);
  or A_C (A_C_out, A, C);
  or B_C (B_C_out, B, C);
  or F (F___C___ABD_prime, C, ABD_prime_out);
  and F_2 (out_6, not_1_out, A_C_out, B_C_out);

  // Notes on the sheet:
  //   Minimal SOP ve POS değerlerini bulup, devrelerini tasarlayalım.
  //   bu kombinasyon önemsenmeyen durumdur. Ayrıca bakım modunda sıcaklık/ nem alarmı da devre dışı bırakılır.
  //   F = D'(A + C)(B+C)
  //   F(A, B, C, D) = Σ(2,6,10,12,14), 𝑑(A, B, C, D)=Σ(3,7,11,15)
  //   F(A, B, C, D) = π(0,1,4,5,8,9,13), 𝑑(A, B, C, D)=Σ(3,7,11,15)
  //   Problem: Bir depo, sıcaklık sensörü (𝐴), nem sensörü (𝐵), gaz sızıntısı sensörü (𝐶) ve bakım modu (𝐷) ile izleniyor. Alarm, bakım modunda değilken (𝐷 = 0) iki durumdan biri gerçekleştiğinde çalar (𝐹 = 1): gaz sızıntısı algılandığında (𝐶 = 1),
  //   ya da sıcaklık ile nem ikisi birden yüksek olduğunda (𝐴 = 1 ve 𝐵 = 1). Bakım sırasında (𝐷 = 1) teknisyen gaz hattını önceden kapattığından, gaz sızıntısı sensörünün (𝐶 = 1) aynı anda aktif olduğu bir durum hiç kaydedilmemiştir;
endmodule
