// Logisim project alistirma-3.11-guvenlik-isigi-sistemi.circ as structural Verilog: 1 circuit, main circuit alistirma-3.11-akilli-guvenlik-isigi
module alistirma_3_11_akilli_guvenlik_isigi (
  input  A,
  input  B,
  input  C,
  input  D,
  output out_5,
  output F___A___C___D
);

  wire AB_out, BC_out, BD_out;

  and AB (AB_out, A, B);
  and BD (BD_out, B, D);
  and BC (BC_out, B, C);
  or A_C_D (F___A___C___D, A, C, D);
  or F (out_5, AB_out, BD_out, BC_out);

  // Notes on the sheet:
  //   Minimal SOP ve POS değerlerini bulup, devrelerini tasarlayalım.
  //   bu durumda hangi kapıların açık olduğu bilinmiyor, yani önemsenmeyen durumdur.
  //   gündüzken (𝐴 = 0) ise yalnızca kapılardan en az biri açık olduğunda (𝐶 = 1 ya da 𝐷 = 1) yanar. Hareket sensörü pasifken (𝐵 = 0), enerji tasarrufu için kapı sensörleri hiç okunmaz;
  //   F = AB + BD + BC
  //   F(A, B, C, D) = π(4), 𝑑(A, B, C, D)=Σ(0,1,2,3,8,9,10,11)
  //   Problem: Bir binanın güvenlik ışığı sistemi 4 sinyal okur: 𝐴 = gece modu, 𝐵 = hareket sensörü aktif, 𝐶 = ön kapı açık, 𝐷 = arka kapı açık. Işık yalnızca hareket algılandığında (𝐵 = 1) yanabilir (𝐹 = 1): gece modundaysa (𝐴 = 1) koşulsuz yanar,
  //   F(A, B, C, D) = Σ(5,6,7,12,13,14,15), 𝑑(A, B, C, D)=Σ(0,1,2,3,8,9,10,11)
endmodule
