// Logisim project ornek-3.14-onluk-yuvarlama-sinyali.circ as structural Verilog: 1 circuit, main circuit ornek-3.14-ondalik-yuvarlama-sinyali
module ornek_3_14_ondalik_yuvarlama_sinyali (
  input  A,
  input  B,
  input  C,
  input  D,
  output out_5,
  output out_6
);

  wire A_B_out, A_C_D_out, BC_out, BD_out;

  and BD (BD_out, B, D);
  and BC (BC_out, B, C);
  or A_B (A_B_out, A, B);
  or A_C_D (A_C_D_out, A, C, D);
  or F (out_5, A, BD_out, BC_out);
  and F_2 (out_6, A_B_out, A_C_D_out);

  // Notes on the sheet:
  //   Minimal SOP ve POS değerlerini bulup, devrelerini tasarlayalım.
  //   Problem: Bir hesap makinesinin ondalık yuvarlama devresi, BCD kodlu tek bir haneyi (𝐴𝐵𝐶𝐷, 𝐴 en anlamlı bit) okuyup, o hane 5 veya daha büyükse yukarı yuvarlama sinyali üretir (𝐹 = 1).
  //   F = A + BD + BC
  //   F = (A + B)(A + C + D)
  //   F(A, B, C, D) = Σ(5,6,7,8,9),  𝑑(A, B, C, D) = Σ(10,11,12,13,14,15)
  //   F(A, B, C, D) = π(0,1,2,3,4),  𝑑(A, B, C, D) = Σ(10,11,12,13,14,15)
endmodule
