// Logisim project ornek-3.15-guvenlik-kapisi-otomatik-kilit.circ as structural Verilog: 1 circuit, main circuit ornek-3.15-guvenlik-kapisi-otomatik-kilit-sistemi
module ornek_3_15_guvenlik_kapisi_otomatik_kilit_sistemi (
  input  A,
  input  B,
  input  C,
  input  D,
  output F___A___C_prime_D,
  output F___C_prime_A___D
);

  wire A_D_out, C_prime_D_out, not_1_out;

  not not_1 (not_1_out, C);
  and C_prime_D (C_prime_D_out, not_1_out, D);
  or A_D (A_D_out, A, D);
  or F (F___A___C_prime_D, A, C_prime_D_out);
  and F_2 (F___C_prime_A___D, not_1_out, A_D_out);

  // Notes on the sheet:
  //   Minimal SOP ve POS değerlerini bulup, devrelerini tasarlayalım.
  //   bakım modunda değilken manuel açma butonuna basıldığında (𝐶 = 0 ve 𝐷 = 1). Gece modunun (𝐵) bu karara hiçbir etkisi yoktur; kilit mantığı gece ile gündüzü ayırt etmez.
  //   Bakım modundayken (𝐶 = 1) yangın alarmı sensörü güvenlik gereği devre dışı bırakılır. Bu yüzden 𝐴 = 1 ile 𝐶 = 1’in aynı anda gerçekleştiği bir durum hiç yaşanmaz.
  //   F(A, B, C, D) = Σ(1,5,8,9,12,13), 𝑑(A, B, C, D)=Σ(10,11,14,15)
  //   F(A, B, C, D) = π(0,2,3,4,6,7), 𝑑(A, B, C, D)=Σ(10,11,14,15)
  //   Problem: Bir güvenlik kapısının otomatik kilit açma devresi 4 sinyal okur: 𝐴 = yan gın alarmı aktif, 𝐵 = gece modu, 𝐶 = bakım modu, 𝐷 = manuel açma butonuna basıldı. Devre kilidi iki durumda açar (𝐹 = 1): yangın alarmı aktif olduğunda (𝐴 = 1), ya da
endmodule
