// Logisim project alistirma-3.12-bahce-guvenlik-aydinlatmasi.circ as structural Verilog: 1 circuit, main circuit alistirma-3.12-akilli-bahce-güvenlik-aydinlatmasi
module \alistirma_3_12_akilli_bahce_güvenlik_aydinlatmasi  (
  input  A,
  input  B,
  input  C,
  output F___A_prime___BC,
  output F____A_BC__prime__prime
);

  wire BC__prime_out, BC_out, not_1_out;

  not not_1 (not_1_out, A);
  and BC (BC_out, B, C);
  nand BC__prime (BC__prime_out, B, C);
  or F (F___A_prime___BC, not_1_out, BC_out);
  nand F_2 (F____A_BC__prime__prime, A, BC__prime_out);

  // Notes on the sheet:
  //   ya da gündüzken bile hem hareket hem ses algılanıyorsa (𝐵 = 1 ve 𝐶 = 1, güvenlik amaçlı).
  //   Minimal SOP değerini bulup, AND-OR kapılarıyla ve NAND kapılarıyla  iki devre tasarlayalım.
  //   F(A, B, C) = Σ(0,1,2,3,7)
  //   F(A, B, C) = Σ(0,1,2,3,7)
  //   Problem: Bir bahçe güvenlik aydınlatması 3 sinyal okur: 𝐴 = gündüz sensörü (1=gündüz), 𝐵 = hareket sensörü, 𝐶 = ses sensörü. Işıklar yanar (𝐹 = 1): gece ise (𝐴 = 0, yani 𝐴′ = 1) her zaman yanar,
endmodule
