// Logisim project alistirma-3.13-montaj-hatti-konveyor-bandi.circ as structural Verilog: 1 circuit, main circuit alistirma-3.13-akilli-konveyor-bandi
module alistirma_3_13_akilli_konveyor_bandi (
  input  A,
  input  B,
  input  C,
  output F___A_B___C,
  output out_5
);

  wire A_prime_out, B_C__prime_out, B_C_out;

  or B_C (B_C_out, B, C);
  nor A_prime (A_prime_out, A, A);
  nor B_C__prime (B_C__prime_out, B, C);
  and F (F___A_B___C, A, B_C_out);
  nor F_2 (out_5, A_prime_out, B_C__prime_out);

  // Notes on the sheet:
  //   Minimal POS değerini bulup, AND-OR kapılarıyla ve NAND kapılarıyla  iki devre tasarlayalım.
  //   Bant, yalnızca ana güç açıkken (𝐴 = 1) ve bandın herhangi bir tarafında hareket algılandığında (𝐵 = 1 ya da 𝐶 = 1) çalışır (𝐹 = 1).
  //   Problem: Bir montaj hattı konveyör bandı 3 sinyal okur: 𝐴 = ana güç anahtarı aktif, 𝐵 = bandın sol tarafındaki hareket sensörü, 𝐶 = bandın sağ tarafındaki hareket sensörü.
  //   F(A, B, C) = Σ(5,6,7)
  //   F(A, B, C) = Σ(5,6,7)
  //   F = (A' + (B + C)')'
endmodule
