// Logisim project alistirma-3.15-tank-basinc-olcer.circ as structural Verilog: 1 circuit, main circuit alistirma-3.15-tank-basinc-olcer.circ
module alistirma_3_15_tank_basinc_olcer_circ (
  input  A,
  input  B,
  output F____A___B__prime
);

  xnor F (F____A___B__prime, A, B);

  // Notes on the sheet:
  //   Sensörler uyuştuğunda sistem bir onay sinyali (𝐹 = 1) üretsin.
  //   F ’i XOR ya da XNOR cinsinden ifade edip devresini tasarlayalım.
  //   Problem: Bir tanktaki sıvı seviyesi, birbirinden bağımsız çalışan iki basınç sensörüyle (𝐴 ve 𝐵) ölçülüyor; ikisi de aynı seviyeyi (yüksek ya da düşük) okumalıdır.
  //   Çözüm: F = 1 olması gereken durum, A ile B’nin aynı değeri aldığı durumdur; bu tam olarak XNOR’un tanımıdır.
endmodule
