// Logisim project alistirma-3.16-kalite-kontrol-sistemi.circ as structural Verilog: 1 circuit, main circuit alistirma-3.16-kalite-kontrol-sistemi
module alistirma_3_16_kalite_kontrol_sistemi (
  input  A,
  input  B,
  input  C,
  input  D,
  output out_5
);

  wire A_B_C_out, A_B_out;

  xor A_B (A_B_out, A, B);
  xor A_B_C (A_B_C_out, A_B_out, C);
  xor F (out_5, A_B_C_out, D);

  // Notes on the sheet:
  //   F ’i kademeli XOR cinsinden ifade edip devresini tasarlayalım.
  //   Problem: Bir montaj hattında 4 istasyon, kendi görevini tamamladığında birer sinyal (𝐴, 𝐵, 𝐶, 𝐷) gönderir. Hat tasarımı gereği normal çalışmada bu sinyallerden çift sayıda tanesi aynı anda aktif olur.
  //   Kalite kontrol sistemi bunu doğrulamak için 𝐴, 𝐵, 𝐶, 𝐷 arasından 1 değerini alanların sayısını kontrol eder: bu sayı tek ise (yani 1 ya da 3 istasyon aktifse) tutarsız bir durum algılanmış demektir ve bir uyarı (𝐹 = 1) üretilir.
  //   F = A ⊕ B ⊕ C ⊕ D
  //   Çözüm: ”Tek sayıda giriş 1” tanımı, doğrudan 4-değişkenli tek sayı fonksiyonuna karşılık gelir.
endmodule
