// Logisim project ornek-3.19-cift-sensor-uyusmazlik-alarmi.circ as structural Verilog: 1 circuit, main circuit ornek-3.19-cift-sensor-uyusmazlik-alarmi
module ornek_3_19_cift_sensor_uyusmazlik_alarmi (
  input  A,
  input  B,
  output F___A___B
);

  xor F (F___A___B, A, B);

  // Notes on the sheet:
  //   F fonksiyonunu veren devreyi tasarlayalım.
  //   Yalnızca birinin tetiklenmesi, sensörlerden birinde bir arıza olduğunu ya da izleme alanına yalnızca kısmi bir müdahale olduğunu gösterir. Sistem bu uyuşmazlığı yakalayıp bir alarm sinyali (𝐹 = 1) üretsin.
  //   Problem: Bir güvenlik sisteminde aynı koridoru izleyen iki bağımsız hareket sensörü var: 𝐴 ve 𝐵. Sistem tasarımına göre bu iki sensör her zaman birlikte hareket etmelidir; ikisi de aynı anda tetiklenmeli ya da ikisi de sakin kalmalıdır.
  //   Çözüm: F = 1 olması gereken tek durum, A ile B’nin farklı değer aldığı durumdur; bu tam olarak XOR’un tanımıdır.
endmodule
