// Logisim project ornek-3.20-hava-istasyonu-parity-uretici-denetleyici.circ as structural Verilog: 1 circuit, main circuit ornek-3.20-hava-istasyonu-parity-uretici-denetleyici
module ornek_3_20_hava_istasyonu_parity_uretici_denetleyici (
  input  x,
  input  y,
  input  z,
  input  HATA_VAR,
  output P___x___y___z,
  output out_6
);

  wire x___y_2_out, x___y_out, x_y_z_out, xor_1_out;

  xor x___y (x___y_out, x, y);
  xor x___y_2 (x___y_2_out, x, y);
  xor P (P___x___y___z, x___y_out, z);
  xor x_y_z (x_y_z_out, x___y_2_out, z);
  xor xor_1 (xor_1_out, P___x___y___z, HATA_VAR);
  xor C (out_6, xor_1_out, x_y_z_out);

  // Notes on the sheet:
  //   İletim hatalarını yakalamak için istasyon çift-parity biti 𝑃 ekliyor, merkez de gelen 4 biti denetliyor.
  //   İstasyondaki parity üreteci ve merkezdeki parity denetleyicisi devrelerini tasarlayalım.
  //   HATA_VAR: P'yi tersine çevirip hata simüle eder → C = HATA_VAR
  //   Problem: Bir uzak hava istasyonu, 3 bitlik bir durum kodunu (𝑥 = pil seviyesi düşük, 𝑦 = sensör arızası var, 𝑧 = bağlantı zayıf; her biri 1=evet) kablosuz olarak merkeze gönderiyor.
  //   C = x ⊕ y ⊕ z ⊕ P
endmodule
