// Logisim project ornek-3.10-uc-kisilik-oylama-sistemi.circ as structural Verilog: 1 circuit, main circuit ornek-3.10-uc-kisilik-oylama-sistemi
module ornek_3_10_uc_kisilik_oylama_sistemi (
  input  x,
  input  y,
  input  z,
  output F___yz___xz___xy
);

  wire xy_out, xz_out, yz_out;

  and yz (yz_out, y, z);
  and xz (xz_out, x, z);
  and xy (xy_out, x, y);
  or F (F___yz___xz___xy, yz_out, xz_out, xy_out);

  // Notes on the sheet:
  //   Problem: Üç kişilik bir yönetim kurulunda 𝑥,𝑦,𝑧 değişkenleri sırasıyla her üyenin oyunu temsil ediyor (1=”evet”, 0=”hayır”). Bir teklifin kabul edilmesi için en az iki üye nin ”evet” demesi gerekiyor. Kurulun kararını (𝐹 = 1: kabul, 𝐹 = 0: ret) veren bir devre tasarlayalım.
endmodule
