// Logisim project ornek-3.11-gecersiz-bcd-kodu-dedektoru.circ as structural Verilog: 1 circuit, main circuit ornek-3.9-asal-sayi-detektoru
module ornek_3_9_asal_sayi_detektoru (
  input  A,
  input  B,
  input  C,
  input  D,
  output F___AB___AC
);

  wire AB_out, AC_out;

  and AB (AB_out, A, B);
  and AC (AC_out, A, C);
  or F (F___AB___AC, AB_out, AC_out);

  // Notes on the sheet:
  //   Girişteki 4 bitlik kodun geçersiz bir BCD basamağı olup olmadığını denetleyen (𝐹 = 1: geçersiz, 𝐹 = 0: geçerli) bir devre tasarlayalım.
  //   Problem: BCD (İkili Kodlanmış Ondalık) sisteminde her ondalık basamak (0-9) 4 bitlik bir ikili kodla (𝐴𝐵𝐶𝐷) temsil edilir. Ama 4 bit ile 0-15 arası 16 farklı değer ifade edilebilir; 10-15 arası değerler BCD standardında kullanılmaz, yani geçersizdir.
endmodule
