// Logisim project ornek-3.9-asal-sayi-detektoru.circ as structural Verilog: 1 circuit, main circuit ornek-3.9-asal-sayi-detektoru
module ornek_3_9_asal_sayi_detektoru (
  input  A,
  input  B,
  input  C,
  input  D,
  output out_5
);

  wire A_prime_B_prime_C_out, A_prime_CD_out, B_prime_CD_out, BC_prime_D_out, not_1_out, not_2_out,
       not_3_out, not_4_out;

  not not_1 (not_1_out, A);
  not not_2 (not_2_out, C);
  not not_3 (not_3_out, B);
  not not_4 (not_4_out, D);
  and A_prime_B_prime_C (A_prime_B_prime_C_out, not_1_out, not_3_out, C);
  and BC_prime_D (BC_prime_D_out, B, not_2_out, D);
  and B_prime_CD (B_prime_CD_out, not_3_out, C, D);
  and A_prime_CD (A_prime_CD_out, not_1_out, C, D);
  or F (out_5, A_prime_B_prime_C_out, BC_prime_D_out, B_prime_CD_out, A_prime_CD_out);

  // Notes on the sheet:
  //   F = A'B'C + BC'D + B'CD + A'CD
  //   Problem: 4 bitlik bir ikili giriş 𝐴𝐵𝐶𝐷 (en anlamlı bit 𝐴), 0 ile 15 arasında bir tam sayıyı temsil ediyor. Bu sayı asal olduğunda çıkışı 𝐹 = 1 yapan, aksi hâlde 𝐹 = 0 veren bir devre tasarlayalım.
endmodule
